// Logisim project exercise_6.circ as structural Verilog: 1 circuit, main circuit main
module main (
  input  in_1,
  input  in_2,
  input  a,
  input  b,
  input  c,
  input  in_6,
  input  in_7,
  input  in_8,
  output out_9,
  output out_10,
  output out_11
);

  wire and_1_out, and_2_out, and_3_out, and_5_out, and_6_out, not_1_out, not_2_out, or_1_out, or_2_out,
       or_3_out;

  not not_1 (not_1_out, in_2);
  not not_2 (not_2_out, in_1);
  or or_1 (or_1_out, in_1, not_1_out);
  or or_2 (or_2_out, not_2_out, in_2);
  or or_3 (or_3_out, a, b);
  and and_1 (and_1_out, in_6, in_8);
  and and_2 (and_2_out, ~in_7, in_8);  // AND_Gate
  and and_3 (and_3_out, ~in_6, in_7, ~in_8);  // AND_Gate
  and and_4 (out_9, or_1_out, or_2_out);
  and and_5 (and_5_out, or_3_out, c);
  or or_4 (out_11, and_1_out, and_2_out, and_3_out);
  and and_6 (and_6_out, ~a, b, ~c);  // AND_Gate
  or or_5 (out_10, and_5_out, and_6_out);
endmodule
