// Logisim project exercise_7.circ as structural Verilog: 4 circuits, main circuit main
module main (
  input  x1_2,
  input  x0_2,
  input  x1_1,
  input  x0_1,
  input  x1_0,
  input  x0_0,
  input  op,
  input  in_8,
  input  in_9,
  input  data,
  input  in_11,
  input  clk,
  output trash,
  output out_14,
  output out_15,
  output out_16,
  output qa
);

  wire fa_2_p4, fa_3_p4, nand_1_out, nand_2_out, xor_1_out, xor_2_out, xor_3_out;

  // fa fa_1: pin names not known; wires that end beside it: trash
  xor xor_1 (xor_1_out, op, x1_2);
  nand nand_1 (nand_1_out, in_8, in_9);
  D_Flip_Flop d_ff_1 (.D(data), .clk(clk), .Q(qa), .reset(in_11));  // open: Qn, preset
  // fa fa_2: pin names not known; wires that end beside it: xor_1_out, out_14, x0_2, fa_2_p4
  nand nand_2 (nand_2_out, nand_1_out, nand_1_out);
  xor xor_2 (xor_2_out, op, x1_1);
  // fa fa_3: pin names not known; wires that end beside it: xor_2_out, out_15, x0_1, fa_3_p4
  xor xor_3 (xor_3_out, op, x1_0);
endmodule

module ha (
  input  x1,
  input  x2,
  output s,
  output c
);

  xor xor_1 (s, x1, x2);
  and and_1 (c, x2, x1);
endmodule

module fa (
  input  x1,
  input  x2,
  input  cin,
  output s,
  output c
);

  wire ha_1_c, ha_1_s, ha_2_c;

  ha ha_1 (.x1(x1), .x2(x2), .s(ha_1_s), .c(ha_1_c));
  ha ha_2 (.x1(ha_1_s), .x2(cin), .s(s), .c(ha_2_c));
  or or_1 (c, ha_1_c, ha_2_c);
endmodule

module sub (
  input  op,
  input  x,
  input  y,
  output out_4,
  output out_5
);

  wire xor_1_out;

  xor xor_1 (xor_1_out, y, op);
  // fa fa_1: pin names not known; wires that end beside it: out_4
endmodule
