// Logisim project serie04.circ as structural Verilog: 1 circuit, main circuit main
module main (
  input  in_1,
  input  critical_path,
  input  in_3
);

  wire and_1_out, and_2_out, not_1_out, not_2_out, not_3_out, or_1_out, or_2_out, pull_resistor_1_node;

  not not_1 (not_1_out, critical_path);
  not not_2 (not_2_out, in_1);
  not not_3 (not_3_out, in_3);
  or or_1 (or_1_out, in_1, not_1_out);
  and and_1 (and_1_out, or_1_out, in_3);
  and and_2 (and_2_out, not_2_out, critical_path, not_3_out);
  or or_2 (or_2_out, and_1_out, and_2_out);
  Pull_Resistor pull_resistor_1 (.node(pull_resistor_1_node));
  // also tied to GND on the sheet: pull_resistor_1_node

  // Notes on the sheet:
  //   p1
  //   critical path
  //   1ff
  //   1ff
  //   critical path
  //   1ff
  //   p2
  //   p3
  //   p4
  //   2 ff
  //   3 ff
  //   2 ff
  //   critical path
  //   p5
  //   p6
  //   1 ff
endmodule
